# Fritzing sketch schema (saved by Fritzing 0.9.3b)
breadboards: 2

parts:
  MH-ET_LIVE_ESP32_DEVKIT1 = MH-ET LIVE ESP32 DEVKIT 38 pins
  DHT1 = DHT11 Humitidy and Temperature Sensor
  DHT2 = DHT11 Humitidy and Temperature Sensor
  PART1 = SparkFun Soil Moisture Sensor [part_number=SEN-13322]
  R1 = Resistor [tolerance=±5% resistance=220 package=THT]
  PART2 = SparkFun Soil Moisture Sensor [part_number=SEN-13322]
  R2 = Resistor [tolerance=±5% resistance=220 package=THT]
  KY-1 = Keyes Relay [package=THT]
  KY-2 = Keyes Relay [package=THT]
  F1 = Fan - Ventilador [package=THT]
  VCC1 = Battery
  Composant1 = submersible pump
  LED1 = LED - 5mm [color="Red (633nm)" package="5 mm [THT]"]  # not connected
  SERVO1 = Adafruit Feedback Servo (small)
  SERVO2 = Adafruit Feedback Servo (small)

nets:
  VDD: MH-ET_LIVE_ESP32_DEVKIT1.3V3, DHT1.VDD, DHT2.VDD, PART1.VCC, R1.Pin_1, PART2.VCC, R2.Pin_1
  N1: MH-ET_LIVE_ESP32_DEVKIT1.IO34, PART2.SIG
  N2: MH-ET_LIVE_ESP32_DEVKIT1.IO35, PART1.SIG
  N3: MH-ET_LIVE_ESP32_DEVKIT1.IO25, DHT2.DATA, R2.Pin_0
  N4: MH-ET_LIVE_ESP32_DEVKIT1.IO27, DHT1.DATA, R1.Pin_0
  GND: MH-ET_LIVE_ESP32_DEVKIT1.GND#58, DHT1.GND, DHT2.GND, PART1.GND, PART2.GND
  N5: MH-ET_LIVE_ESP32_DEVKIT1.GND#64, F1.GND, VCC1.-, Composant1.pin1, SERVO1.Ground, SERVO2.Ground
  N6: MH-ET_LIVE_ESP32_DEVKIT1.GND#70, KY-1.ground, KY-2.ground
  N7: MH-ET_LIVE_ESP32_DEVKIT1.IO5, KY-2.signal
  N8: MH-ET_LIVE_ESP32_DEVKIT1.IO17, SERVO1.Signal
  N9: MH-ET_LIVE_ESP32_DEVKIT1.IO16, SERVO2.Signal
  N10: MH-ET_LIVE_ESP32_DEVKIT1.IO4, KY-1.signal
  N11: KY-1.power, KY-2.power
  N12: KY-1.C, KY-2.C, VCC1.+, SERVO1.Power, SERVO2.Power
  N13: KY-1.NO, Composant1.pin2
  N14: KY-2.NO, F1.5V

custom parts:
  MH-ET LIVE ESP32 DEVKIT 38 pins: http://mh.nodebb.com/topic/2/mh-et-live-esp32-devkit
  DHT11 Humitidy and Temperature Sensor: DHT11 Humidity and Temperature Sensor
  SparkFun Soil Moisture Sensor: The SparkFun Soil Moisture Sensor is a simple breakout for measuring the moisture in soil and similar materials.
  Keyes Relay: The Keyes 5V relay module is suitable for SCM development, home appliance control. It uses a 5V~12V TIL control signal which can control DC / AC signal.
  Fan - Ventilador: Ventilador de 2 pines, se encuentra comunmente en computadoras de escritorio
  Battery: Your standard 2x 18650 battery pack (7,4 Volts)
  submersible pump: pump
  Adafruit Feedback Servo (small): Adafruit Feedback Servo (Small)
